# Fritzing sketch Wiring Diagram (saved by Fritzing 0.9.3b)
breadboards: 1

parts:
  Adafruit_HUZZAH_ESP8266_Breakout1 = Adafruit HUZZAH ESP8266 Breakout [part_number=2471]
  U1 = SWITCH_SPDT [package=kps-1290]
  U2 = LIPO-1000mAh [package=lipo-1000]
  T1 = LM35 Temperature Sensor [package="TO92 [THT]"]

nets:
  GND: Adafruit_HUZZAH_ESP8266_Breakout1.GND, U1.S, U2.-, T1.GND
  N1: Adafruit_HUZZAH_ESP8266_Breakout1.VBat, U2.+
  N2: Adafruit_HUZZAH_ESP8266_Breakout1.V+, U1.P, T1.Vout
  N3: Adafruit_HUZZAH_ESP8266_Breakout1.#13, T1.+Vs
  N4: Adafruit_HUZZAH_ESP8266_Breakout1.#12, U1.O

notes:
  Water Sensor
  Speaker
